// Logisim project vigenere_sinito.circ as structural Verilog: 2 circuits, main circuit main
module main (
  input  [7:0] PrimoSimbolo,
  input  [7:0] DimAlfabeto,
  input  CLR,
  input  CODIFICA__0
);

  wire and_1_out, CLK, CLK_out, comparator_1_eq, comparator_2_eq, comparator_3_eq, comparator_3_gt,
       comparator_4_lt, not_1_out, not_2_out, or_1_out, or_2_out;
  wire [7:0] adder_1_out, adder_2_out, CHIAVE_data, contatore_1_out_3, contatore_2_out_3, INGRESSO_data,
       multiplexer_1_out, multiplexer_2_out, multiplexer_3_out, subtractor_1_out, subtractor_2_out,
       subtractor_3_out, subtractor_4_out, USCITA_data;

  Comparator comparator_1 (.a(CHIAVE_data), .b({8{1'b0}}), .eq(comparator_1_eq));  // open: gt, lt
  or or_1 (or_1_out, comparator_1_eq, CLR);
  Contatore contatore_1 (.CLK(CLK), .CLR(CLR), .out_3(contatore_1_out_3));
  ROM CHIAVE (.addr(contatore_2_out_3), .data(CHIAVE_data));
  Contatore contatore_2 (.CLK(CLK), .CLR(or_1_out), .out_3(contatore_2_out_3));
  ROM INGRESSO (.addr(contatore_1_out_3), .data(INGRESSO_data));
  RAM #(.clearpin("true"), .databus("bidir")) USCITA (
    .addr(contatore_1_out_3), .we(1'b1), .oe(1'b0), .clk(CLK), .data(USCITA_data), .clr(CLR));
  Subtractor subtractor_1 (.a(CHIAVE_data), .b(PrimoSimbolo), .out(subtractor_1_out));  // open: bin, bout
  Subtractor subtractor_2 (.a(INGRESSO_data), .b(PrimoSimbolo), .out(subtractor_2_out));  // open: bin, bout
  Subtractor subtractor_3 (.a(INGRESSO_data), .b(CHIAVE_data), .out(subtractor_3_out));  // open: bin, bout
  Adder adder_1 (.a(subtractor_1_out), .b(subtractor_2_out), .out(adder_1_out));  // open: cin, cout
  not not_1 (not_1_out, comparator_2_eq);
  Comparator comparator_2 (.a(INGRESSO_data), .b({8{1'b0}}), .eq(comparator_2_eq));  // open: gt, lt
  Clock u_CLK (.out(CLK_out));
  and and_1 (and_1_out, CLK_out, ~CLR);  // AND_Gate
  and and_2 (CLK, not_1_out, and_1_out);
  Comparator comparator_3 (.a(adder_1_out), .b(DimAlfabeto), .gt(comparator_3_gt), .eq(comparator_3_eq));  // open: lt
  or or_2 (or_2_out, comparator_3_eq, comparator_3_gt);
  Subtractor subtractor_4 (.a(adder_1_out), .b(DimAlfabeto), .out(subtractor_4_out));  // open: bin, bout
  Adder adder_2 (.a(DimAlfabeto), .b(subtractor_3_out), .out(adder_2_out));  // open: cin, cout
  not not_2 (not_2_out, comparator_4_lt);
  Comparator comparator_4 (.a(subtractor_3_out), .b({8{1'b0}}), .lt(comparator_4_lt));  // open: gt, eq
  Multiplexer #(.width(8)) multiplexer_1 (
    .in0(adder_1_out), .in1(subtractor_4_out), .out(multiplexer_1_out), .sel(or_2_out));
  Multiplexer #(.width(8)) multiplexer_2 (
    .in0(adder_2_out), .in1(subtractor_3_out), .out(multiplexer_2_out), .sel(not_2_out));
  Multiplexer #(.width(8)) multiplexer_3 (
    .in0(multiplexer_1_out), .in1(multiplexer_2_out), .out(multiplexer_3_out), .sel(CODIFICA__0));
  Adder adder_3 (.a(multiplexer_3_out), .b(PrimoSimbolo), .out(USCITA_data));  // open: cin, cout

  // Other names for the same wires on the sheet: DimAlfa[7:0] = DimAlfabeto; P_Simb[7:0] = PrimoSimbolo

  // Notes on the sheet:
  //   PrimoSimbolo: initial=0x41
  //   DimAlfabeto: initial=0x1a
  //   CIRCUITO RIPETIZIONE CHIAVE
  //   SELEZIONE CARATTERE
  //   contents of CHIAVE (hex, n*v repeats v):
  //   53 4f 4c 45
  //   contents of INGRESSO (hex, n*v repeats v):
  //   4e 4f 4e 56 45 44 4f 4e 4f 4e 53 45 4e 54 4f 4e 4f 4e 50 41 52 4c 4f
  //   modalita (0) --->
  //   modalita (1) --->
  //   --- MODALITA ---
  //   DECODIFICA (1)
  //   CALCOLO OFFSET
  //   CONTROLLO DEL PROGRAMMA
  //   NORMALIZZAZIONE
  //   SEL. MODALITA
  //   CALC. CARATTERE
endmodule

module Contatore (
  input  CLK,
  input  CLR,
  output [7:0] out_3
);

  T_Flip_Flop #(.trigger("falling")) t_ff_1 (.T(1'b1), .clk(CLK), .Q(out_3[0]), .reset(CLR));  // open: Qn, preset
  T_Flip_Flop #(.trigger("falling")) t_ff_2 (.T(1'b1), .clk(out_3[0]), .Q(out_3[1]), .reset(CLR));  // open: Qn, preset
  T_Flip_Flop #(.trigger("falling")) t_ff_3 (.T(1'b1), .clk(out_3[1]), .Q(out_3[2]), .reset(CLR));  // open: Qn, preset
  T_Flip_Flop #(.trigger("falling")) t_ff_4 (.T(1'b1), .clk(out_3[2]), .Q(out_3[3]), .reset(CLR));  // open: Qn, preset
  T_Flip_Flop #(.trigger("falling")) t_ff_5 (.T(1'b1), .clk(out_3[3]), .Q(out_3[4]), .reset(CLR));  // open: Qn, preset
  T_Flip_Flop #(.trigger("falling")) t_ff_6 (.T(1'b1), .clk(out_3[4]), .Q(out_3[5]), .reset(CLR));  // open: Qn, preset
  T_Flip_Flop #(.trigger("falling")) t_ff_7 (.T(1'b1), .clk(out_3[5]), .Q(out_3[6]), .reset(CLR));  // open: Qn, preset
  T_Flip_Flop #(.trigger("falling")) t_ff_8 (.T(1'b1), .clk(out_3[6]), .Q(out_3[7]), .reset(CLR));  // open: Qn, preset
endmodule
